// Logisim project oclock.circ as structural Verilog: 15 circuits, main circuit main
module main (
);

  wire Add1h, Add1m, Add1s, Ah12A1, Ah12A2, Ah12B1, Ah12B2, Ah12C1, Ah12C2, Ah12D1, Ah12D2, Ah24A1, Ah24A2,
       Ah24B1, Ah24B2, Ah24C1, Ah24C2, Ah24D1, Ah24D2, Alarm, AlarmAdd1h, AlarmAdd1m, AlarmMode, AlarmPower,
       AlarmReset, AM, AM1, AmA1, AmA2, AmB1, AmB2, AmC1, AmC2, AmD1, AmD2, AsA1, AsA2, AsB1, AsB2, AsC1,
       AsC2, AsD1, AsD2, change12or24, Clock, DebugMode, h12A1, h12A2, h12B1, h12B2, h12C1, h12C2, h12D1,
       h12D2, h24A1, h24A2, h24B1, h24B2, h24C1, h24C2, h24D1, h24D2, hA1, ha1_t, hA2, ha2_t, hB1, hb1_t,
       hB2, hb2_t, hC1, hc1_t, hC2, hc2_t, hD1, hd1_t, hD2, hd2_t, hE1, hE2, hF1, hF2, hG1, hG2, io0, io1,
       io2, io3, io4, io5, io6, io7, io9, mA1, ma1_t, mA2, ma2_t, mB1, mb1_t, mB2, mb2_t, mC1, mc1_t, mC2,
       mc2_t, mD1, md1_t, mD2, md2_t, me1, me2, mf1, mf2, mg1, mg2, PM, PM1, Reset, sA1, sa1_t, sA2, sa2_t,
       sB1, sb1_t, sB2, sb2_t, sC1, sc1_t, sC2, sc2_t, sD1, sd1_t, sD2, sd2_t, se1, se2, sf1, sf2, sg1, sg2,
       Sh12A1, Sh12A2, Sh12B1, Sh12B2, Sh12C1, Sh12C2, Sh12D1, Sh12D2, Sh24A1, Sh24A2, Sh24B1, Sh24B2,
       Sh24C1, Sh24C2, Sh24D1, Sh24D2, SmA1, SmA2, SmB1, SmB2, SmC1, SmC2, SmD1, SmD2, SsA1, SsA2, SsB1,
       SsB2, SsC1, SsC2, SsD1, SsD2, Switch, True2, True3, True4;

  LED led_1 (.in(AM));
  LED led_2 (.in(PM));
  _7_Segment_Display u_7_segment_display_1 (.g(hG2), .f(hF2), .a(hA2), .b(hB2), .e(hE2), .d(hD2), .c(hC2));  // open: dp
  _7_Segment_Display u_7_segment_display_2 (
    .g(mg2), .f(mf2), .a(ma2_t), .b(mb2_t), .e(me2), .d(md2_t), .c(mc2_t));  // open: dp
  _7_Segment_Display u_7_segment_display_3 (
    .g(sg2), .f(sf2), .a(sa2_t), .b(sb2_t), .e(se2), .d(sd2_t), .c(sc2_t));  // open: dp
  _7_Segment_Display u_7_segment_display_4 (.g(hG1), .f(hF1), .a(hA1), .b(hB1), .e(hE1), .d(hD1), .c(hC1));  // open: dp
  _7_Segment_Display u_7_segment_display_5 (
    .g(mg1), .f(mf1), .a(ma1_t), .b(mb1_t), .e(me1), .d(md1_t), .c(mc1_t));  // open: dp
  _7_Segment_Display u_7_segment_display_6 (
    .g(sg1), .f(sf1), .a(sa1_t), .b(sb1_t), .e(se1), .d(sd1_t), .c(sc1_t));  // open: dp
  Button button_1 (.out(Reset));
  Button button_2 (.out(Add1h));
  Button button_3 (.out(Add1m));
  Button button_4 (.out(Add1s));
  // DipSwitch #(.number(1)) dipswitch_1: pin names not known; wires that end beside it: Switch
  // DipSwitch #(.number(1)) dipswitch_2: pin names not known; wires that end beside it: change12or24
  // DipSwitch #(.number(1)) dipswitch_3: pin names not known; wires that end beside it: DebugMode
  LED led_3 (.in(Alarm));
  // DipSwitch #(.number(1)) dipswitch_4: pin names not known; wires that end beside it: AlarmPower
  // DipSwitch #(.number(1)) dipswitch_5: pin names not known; wires that end beside it: AlarmMode
  Button button_5 (.out(AlarmAdd1h));
  Button button_6 (.out(AlarmAdd1m));
  Button button_7 (.out(AlarmReset));
  j10 j10_1 (.CLOCK(io0), .Reset(Reset), .A(SsA1), .B(SsB1), .C(SsC1), .D(SsD1), .out1(io1));
  j6 j6_1 (.in1(io1), .Reset(Reset), .A(SsA2), .B(SsB2), .C(SsC2), .D(SsD2), .out2(io2));
  j10 j10_2 (.CLOCK(io3), .Reset(Reset), .A(SmA1), .B(SmB1), .C(SmC1), .D(SmD1), .out1(io4));
  j6 j6_2 (.in1(io4), .Reset(Reset), .A(SmA2), .B(SmB2), .C(SmC2), .D(SmD2), .out2(io5));
  j10 j10_3 (.Reset(AlarmReset), .A(AsA1), .B(AsB1), .C(AsC1), .D(AsD1), .out1(io7));  // open: CLOCK
  j12new j12new_1 (
    .in1(io6), .Reset(Reset), .Switch(Switch), .A1(Sh12A1), .B1(Sh12B1), .C1(Sh12C1), .D1(Sh12D1),
    .A2(Sh12A2), .B2(Sh12B2), .C2(Sh12C2), .D2(Sh12D2), .AM(AM1), .PM(PM1));
  j24 j24_1 (
    .in1(io6), .Reset(Reset), .A1(Sh24A1), .B1(Sh24B1), .C1(Sh24C1), .D1(Sh24D1), .A2(Sh24A2), .B2(Sh24B2),
    .C2(Sh24C2), .D2(Sh24D2));
  j6 j6_3 (.in1(io7), .Reset(AlarmReset), .A(AsA2), .B(AsB2), .C(AsC2), .D(AsD2));  // open: out2
  AlarmS alarms_1 (
    .Ctrl(AlarmMode), .AsA1(AsA1), .AsA2(AsA2), .SsA1(SsA1), .SsA2(SsA2), .AsB1(AsB1), .AsB2(AsB2),
    .SsB1(SsB1), .SsB2(SsB2), .AsC1(AsC1), .AsC2(AsC2), .SsC1(SsC1), .SsC2(SsC2), .AsD1(AsD1), .AsD2(AsD2),
    .SsD1(SsD1), .SsD2(SsD2), .sA1(sA1), .sA2(sA2), .sB1(sB1), .sB2(sB2), .sC1(sC1), .sC2(sC2), .sD1(sD1),
    .sD2(sD2));
  Alarm1 alarm1_1 (
    .SA1(SmA1), .AA1(AmA1), .SB1(SmB1), .AB1(AmB1), .SC1(SmC1), .AC1(AmC1), .SD1(SmD1), .AP(AlarmPower),
    .AD1(AmD1), .SA2(SmA2), .AA2(AmA2), .SB2(SmB2), .AB2(AmB2), .SC2(SmC2), .AC2(AmC2), .SD2(SmD2),
    .AD2(AmD2), .TRUE(True2));
  YiMaQi yimaqi_1 (
    .DD(sD1), .CC(sC1), .BB(sB1), .AA(sA1), .a(sa1_t), .b(sb1_t), .c(sc1_t), .d(sd1_t), .e(se1), .f(sf1),
    .g(sg1));
  YiMaQi yimaqi_2 (
    .DD(sD2), .CC(sC2), .BB(sB2), .AA(sA2), .a(sa2_t), .b(sb2_t), .c(sc2_t), .d(sd2_t), .e(se2), .f(sf2),
    .g(sg2));
  YiMaQi yimaqi_3 (
    .DD(mD1), .CC(mC1), .BB(mB1), .AA(mA1), .a(ma1_t), .b(mb1_t), .c(mc1_t), .d(md1_t), .e(me1), .f(mf1),
    .g(mg1));
  YiMaQi yimaqi_4 (
    .DD(mD2), .CC(mC2), .BB(mB2), .AA(mA2), .a(ma2_t), .b(mb2_t), .c(mc2_t), .d(md2_t), .e(me2), .f(mf2),
    .g(mg2));
  AlarmM alarmm_1 (
    .Ctrl(AlarmMode), .AmA1(AmA1), .AmA2(AmA2), .SmA1(SmA1), .SmA2(SmA2), .AmB1(AmB1), .AmB2(AmB2),
    .SmB1(SmB1), .SmB2(SmB2), .AmC1(AmC1), .AmC2(AmC2), .SmC1(SmC1), .SmC2(SmC2), .AmD1(AmD1), .AmD2(AmD2),
    .SmD1(SmD1), .SmD2(SmD2), .mA1(mA1), .mA2(mA2), .mB1(mB1), .mB2(mB2), .mC1(mC1), .mC2(mC2), .mD1(mD1),
    .mD2(mD2));
  Alarm1 alarm1_2 (
    .SA1(Sh12A1), .AA1(Ah12A1), .SB1(Sh12B1), .AB1(Ah12B1), .SC1(Sh12C1), .AC1(Ah12C1), .SD1(Sh12D1),
    .AP(AlarmPower), .AD1(Ah12D1), .SA2(Sh12A2), .AA2(Ah12A2), .SB2(Sh12B2), .AB2(Ah12B2), .SC2(Sh12C2),
    .AC2(Ah12C2), .SD2(Sh12D2), .AD2(Ah12D2), .TRUE(True3));
  choose12or24 choose12or24_1 (
    .Ctrl(change12or24), .h12a1(h12A1), .h12a2(h12A2), .h24a1(h24A1), .h24a2(h24A2), .h12b1(h12B1),
    .h12b2(h12B2), .h24b1(h24B1), .h24b2(h24B2), .h12c1(h12C1), .h12c2(h12C2), .h24c1(h24C1), .h24c2(h24C2),
    .h12d1(h12D1), .h12d2(h12D2), .h24d1(h24D1), .h24d2(h24D2), .ha1(ha1_t), .ha2(ha2_t), .hb1(hb1_t),
    .hb2(hb2_t), .hc1(hc1_t), .hc2(hc2_t), .hd1(hd1_t), .hd2(hd2_t));
  j10 j10_4 (.CLOCK(AlarmAdd1m), .Reset(AlarmReset), .A(AmA1), .B(AmB1), .C(AmC1), .D(AmD1), .out1(io9));
  j6 j6_4 (.in1(io9), .Reset(AlarmReset), .A(AmA2), .B(AmB2), .C(AmC2), .D(AmD2));  // open: out2
  AlarmH alarmh_1 (
    .Ctrl(AlarmMode), .AhA1(Ah12A1), .AhA2(Ah12A2), .ShA1(Sh12A1), .ShA2(Sh12A2), .AhB1(Ah12B1),
    .AhB2(Ah12B2), .ShB1(Sh12B1), .ShB2(Sh12B2), .AhC1(Ah12C1), .AhC2(Ah12C2), .ShC1(Sh12C1), .ShC2(Sh12C2),
    .AhD1(Ah12D1), .AhD2(Ah12D2), .ShD1(Sh12D1), .ShD2(Sh12D2), .hA1(h12A1), .hA2(h12A2), .hB1(h12B1),
    .hB2(h12B2), .hC1(h12C1), .hC2(h12C2), .hD1(h12D1), .hD2(h12D2));
  Alarm1 alarm1_3 (
    .SA1(Sh24A1), .AA1(Ah24A1), .SB1(Sh24B1), .AB1(Ah24B1), .SC1(Sh24C1), .AC1(Ah24C1), .SD1(Sh24D1),
    .AP(AlarmPower), .AD1(Ah24D1), .SA2(Sh24A2), .AA2(Ah24A2), .SB2(Sh24B2), .AB2(Ah24B2), .SC2(Sh24C2),
    .AC2(Ah24C2), .SD2(Sh24D2), .AD2(Ah24D2), .TRUE(True4));
  ClockSwitch clockswitch_1 (.inin(Switch), .outout(Clock));
  YiMaQi yimaqi_5 (
    .DD(hd1_t), .CC(hc1_t), .BB(hb1_t), .AA(ha1_t), .a(hA1), .b(hB1), .c(hC1), .d(hD1), .e(hE1), .f(hF1),
    .g(hG1));
  YiMaQi yimaqi_6 (
    .DD(hd2_t), .CC(hc2_t), .BB(hb2_t), .AA(ha2_t), .a(hA2), .b(hB2), .c(hC2), .d(hD2), .e(hE2), .f(hF2),
    .g(hG2));
  j12new j12new_2 (
    .in1(AlarmReset), .Reset(AlarmAdd1h), .Switch(Switch), .A1(Ah12A1), .B1(Ah12B1), .C1(Ah12C1),
    .D1(Ah12D1), .A2(Ah12A2), .B2(Ah12B2), .C2(Ah12C2), .D2(Ah12D2));  // open: AM, PM
  debug debug_1 (.man(Add1s), .Ctrl2(DebugMode), .auto(Clock), .\final (io0));
  debug debug_2 (.man(Add1m), .Ctrl2(DebugMode), .auto(io2), .\final (io3));
  debug debug_3 (.man(Add1h), .Ctrl2(DebugMode), .auto(io5), .\final (io6));
  AlarmH alarmh_2 (
    .Ctrl(AlarmMode), .AhA1(Ah24A1), .AhA2(Ah24A2), .ShA1(Sh24A1), .ShA2(Sh24A2), .AhB1(Ah24B1),
    .AhB2(Ah24B2), .ShB1(Sh24B1), .ShB2(Sh24B2), .AhC1(Ah24C1), .AhC2(Ah24C2), .ShC1(Sh24C1), .ShC2(Sh24C2),
    .AhD1(Ah24D1), .AhD2(Ah24D2), .ShD1(Sh24D1), .ShD2(Sh24D2), .hA1(h24A1), .hA2(h24A2), .hB1(h24B1),
    .hB2(h24B2), .hC1(h24C1), .hC2(h24C2), .hD1(h24D1), .hD2(h24D2));
  AlarmTrue alarmtrue_1 (.True2(True2), .True3(True3), .True4(True4), .led(Alarm));
  ShowAMorPM showamorpm_1 (
    .AM1(AM1), .only12(change12or24), .PM1(PM1), .Switch(Switch), .Alarm(AlarmPower), .AM(AM), .PM(PM));
  j24 j24_2 (
    .in1(AlarmAdd1h), .Reset(AlarmReset), .A1(Ah24A1), .B1(Ah24B1), .C1(Ah24C1), .D1(Ah24D1), .A2(Ah24A2),
    .B2(Ah24B2), .C2(Ah24C2), .D2(Ah24D2));

  // Notes on the sheet:
  //   秒计时器
  //   分计时器
  //   闹钟系统
  //   时计时器（包含12/24切换）
  //   调试系统
  //   闹钟总开关
endmodule

module YiMaQi (
  input  DD,
  input  CC,
  input  BB,
  input  AA,
  output a,
  output b,
  output c,
  output d,
  output e,
  output f,
  output g
);

  wire and_1_out, and_2_out, and_3_out, and_4_out, and_5_out, and_6_out, and_7_out, and_8_out, and_9_out,
       and_10_out, and_11_out, and_12_out, and_13_out, and_14_out, and_15_out, and_16_out, not_1_out,
       not_2_out, not_3_out;

  not not_1 (not_1_out, CC);
  not not_2 (not_2_out, BB);
  not not_3 (not_3_out, AA);
  and and_1 (and_1_out, not_1_out, not_3_out);
  and and_2 (and_2_out, CC, AA);
  and and_3 (and_3_out, not_2_out, not_3_out);
  and and_4 (and_4_out, BB, AA);
  or or_1 (c, not_2_out, AA, CC);
  and and_5 (and_5_out, not_1_out, not_3_out);
  and and_6 (and_6_out, not_1_out, BB);
  and and_7 (and_7_out, CC, not_2_out, AA);
  and and_8 (and_8_out, BB, not_3_out);
  and and_9 (and_9_out, not_1_out, not_3_out);
  and and_10 (and_10_out, BB, not_3_out);
  and and_11 (and_11_out, not_2_out, not_3_out);
  and and_12 (and_12_out, CC, not_2_out);
  and and_13 (and_13_out, CC, not_3_out);
  and and_14 (and_14_out, not_1_out, BB);
  and and_15 (and_15_out, CC, not_2_out);
  and and_16 (and_16_out, BB, not_3_out);
  or or_2 (a, and_1_out, BB, and_2_out, DD);
  or or_3 (b, not_1_out, and_3_out, and_4_out);
  or or_4 (d, and_5_out, and_6_out, and_7_out, and_8_out, DD);
  or or_5 (e, and_9_out, and_10_out);
  or or_6 (f, and_11_out, and_12_out, and_13_out, DD);
  or or_7 (g, and_14_out, and_15_out, DD, and_16_out);
endmodule

module j10 (
  input  CLOCK,
  input  Reset,
  output A,
  output B,
  output C,
  output D,
  output out1
);

  wire or_1_out;

  J_K_Flip_Flop #(.trigger("falling")) j_k_ff_1 (
    .J(1'b1), .K(1'b1), .clk(CLOCK), .Q(A), .reset(or_1_out));  // open: Qn, preset
  J_K_Flip_Flop #(.trigger("falling")) j_k_ff_2 (
    .J(1'b1), .K(1'b1), .clk(A), .Q(B), .reset(or_1_out));  // open: Qn, preset
  or or_1 (or_1_out, Reset, out1);
  J_K_Flip_Flop #(.trigger("falling")) j_k_ff_3 (
    .J(1'b1), .K(1'b1), .clk(B), .Q(C), .reset(or_1_out));  // open: Qn, preset
  and and_1 (out1, B, D);
  J_K_Flip_Flop #(.trigger("falling")) j_k_ff_4 (
    .J(1'b1), .K(1'b1), .clk(C), .Q(D), .reset(or_1_out));  // open: Qn, preset
endmodule

module j6 (
  input  in1,
  input  Reset,
  output A,
  output B,
  output C,
  output D,
  output out2
);

  wire or_1_out;

  J_K_Flip_Flop #(.trigger("falling")) j_k_ff_1 (
    .J(1'b1), .K(1'b1), .clk(in1), .Q(A), .reset(or_1_out));  // open: Qn, preset
  J_K_Flip_Flop #(.trigger("falling")) j_k_ff_2 (
    .J(1'b1), .K(1'b1), .clk(A), .Q(B), .reset(or_1_out));  // open: Qn, preset
  or or_1 (or_1_out, Reset, out2);
  J_K_Flip_Flop #(.trigger("falling")) j_k_ff_3 (
    .J(1'b1), .K(1'b1), .clk(B), .Q(C), .reset(or_1_out));  // open: Qn, preset
  and and_1 (out2, B, C);
  J_K_Flip_Flop #(.trigger("falling")) j_k_ff_4 (
    .J(1'b1), .K(1'b1), .clk(C), .Q(D), .reset(or_1_out));  // open: Qn, preset
endmodule

module j24 (
  input  in1,
  input  Reset,
  output A1,
  output B1,
  output C1,
  output D1,
  output A2,
  output B2,
  output C2,
  output D2
);

  wire and_1_out, and_2_out, and_3_out, or_1_out, or_2_out;

  J_K_Flip_Flop #(.trigger("falling")) j_k_ff_1 (
    .J(1'b1), .K(1'b1), .clk(in1), .Q(A1), .reset(or_1_out));  // open: Qn, preset
  J_K_Flip_Flop #(.trigger("falling")) j_k_ff_2 (
    .J(1'b1), .K(1'b1), .clk(A1), .Q(B1), .reset(or_1_out));  // open: Qn, preset
  J_K_Flip_Flop #(.trigger("falling")) j_k_ff_3 (
    .J(1'b1), .K(1'b1), .clk(B1), .Q(C1), .reset(or_1_out));  // open: Qn, preset
  or or_1 (or_1_out, and_2_out, Reset, and_1_out);
  and and_1 (and_1_out, B1, D1);
  and and_2 (and_2_out, C1, B2);
  J_K_Flip_Flop #(.trigger("falling")) j_k_ff_4 (
    .J(1'b1), .K(1'b1), .clk(C1), .Q(D1), .reset(or_1_out));  // open: Qn, preset
  and and_3 (and_3_out, C1, B2);
  J_K_Flip_Flop #(.trigger("falling")) j_k_ff_5 (
    .J(1'b1), .K(1'b1), .clk(and_1_out), .Q(A2), .reset(or_2_out));  // open: Qn, preset
  J_K_Flip_Flop #(.trigger("falling")) j_k_ff_6 (
    .J(1'b1), .K(1'b1), .clk(A2), .Q(B2), .reset(or_2_out));  // open: Qn, preset
  or or_2 (or_2_out, Reset, and_3_out);
  J_K_Flip_Flop #(.trigger("falling")) j_k_ff_7 (
    .J(1'b1), .K(1'b1), .clk(B2), .Q(C2), .reset(or_2_out));  // open: Qn, preset
  J_K_Flip_Flop #(.trigger("falling")) j_k_ff_8 (
    .J(1'b1), .K(1'b1), .clk(C2), .Q(D2), .reset(or_2_out));  // open: Qn, preset

  // Other names for the same wires on the sheet: Reset000 = Reset
endmodule

module choose12or24 (
  input  Ctrl,
  input  h12a1,
  input  h12a2,
  input  h24a1,
  input  h24a2,
  input  h12b1,
  input  h12b2,
  input  h24b1,
  input  h24b2,
  input  h12c1,
  input  h12c2,
  input  h24c1,
  input  h24c2,
  input  h12d1,
  input  h12d2,
  input  h24d1,
  input  h24d2,
  output ha1,
  output ha2,
  output hb1,
  output hb2,
  output hc1,
  output hc2,
  output hd1,
  output hd2
);

  wire and_1_out, and_2_out, and_3_out, and_4_out, and_5_out, and_6_out, and_7_out, and_8_out, and_9_out,
       and_10_out, and_11_out, and_12_out, and_13_out, and_14_out, and_15_out, and_16_out, not_1_out,
       not_2_out, not_3_out, not_4_out, not_5_out, not_6_out, not_7_out, not_8_out;

  and and_1 (and_1_out, h12a1, Ctrl);
  not not_1 (not_1_out, Ctrl);
  and and_2 (and_2_out, not_1_out, h24a1);
  and and_3 (and_3_out, h12b1, Ctrl);
  not not_2 (not_2_out, Ctrl);
  and and_4 (and_4_out, not_2_out, h24b1);
  and and_5 (and_5_out, h12c1, Ctrl);
  not not_3 (not_3_out, Ctrl);
  and and_6 (and_6_out, not_3_out, h24c1);
  and and_7 (and_7_out, h12d1, Ctrl);
  not not_4 (not_4_out, Ctrl);
  and and_8 (and_8_out, not_4_out, h24d1);
  or or_1 (ha1, and_1_out, and_2_out);
  or or_2 (hb1, and_3_out, and_4_out);
  or or_3 (hc1, and_5_out, and_6_out);
  or or_4 (hd1, and_7_out, and_8_out);
  not not_5 (not_5_out, Ctrl);
  not not_6 (not_6_out, Ctrl);
  not not_7 (not_7_out, Ctrl);
  not not_8 (not_8_out, Ctrl);
  and and_9 (and_9_out, h12a2, Ctrl);
  and and_10 (and_10_out, not_5_out, h24a2);
  and and_11 (and_11_out, h12b2, Ctrl);
  and and_12 (and_12_out, not_6_out, h24b2);
  and and_13 (and_13_out, h12c2, Ctrl);
  and and_14 (and_14_out, not_7_out, h24c2);
  and and_15 (and_15_out, h12d2, Ctrl);
  and and_16 (and_16_out, not_8_out, h24d2);
  or or_5 (ha2, and_9_out, and_10_out);
  or or_6 (hb2, and_11_out, and_12_out);
  or or_7 (hc2, and_13_out, and_14_out);
  or or_8 (hd2, and_15_out, and_16_out);

  // Other names for the same wires on the sheet: iiin = Ctrl
endmodule

module debug (
  input  man,
  input  Ctrl2,
  input  auto,
  output \final 
);

  wire and_1_out, and_2_out, not_1_out;

  not not_1 (not_1_out, Ctrl2);
  and and_1 (and_1_out, man, Ctrl2);
  and and_2 (and_2_out, not_1_out, auto);
  or or_1 (\final , and_1_out, and_2_out);
endmodule

module ClockSwitch (
  input  inin,
  output outout
);

  wire clock_1_out;

  Clock clock_1 (.out(clock_1_out));
  and and_1 (outout, inin, clock_1_out);
endmodule

module AlarmS (
  input  Ctrl,
  input  AsA1,
  input  AsA2,
  input  SsA1,
  input  SsA2,
  input  AsB1,
  input  AsB2,
  input  SsB1,
  input  SsB2,
  input  AsC1,
  input  AsC2,
  input  SsC1,
  input  SsC2,
  input  AsD1,
  input  AsD2,
  input  SsD1,
  input  SsD2,
  output sA1,
  output sA2,
  output sB1,
  output sB2,
  output sC1,
  output sC2,
  output sD1,
  output sD2
);

  wire and_1_out, and_2_out, and_3_out, and_4_out, and_5_out, and_6_out, and_7_out, and_8_out, and_9_out,
       and_10_out, and_11_out, and_12_out, and_13_out, and_14_out, and_15_out, and_16_out, not_1_out,
       not_2_out, not_3_out, not_4_out, not_5_out, not_6_out, not_7_out, not_8_out;

  and and_1 (and_1_out, AsA1, Ctrl);
  not not_1 (not_1_out, Ctrl);
  and and_2 (and_2_out, not_1_out, SsA1);
  and and_3 (and_3_out, AsB1, Ctrl);
  not not_2 (not_2_out, Ctrl);
  and and_4 (and_4_out, not_2_out, SsB1);
  and and_5 (and_5_out, AsC1, Ctrl);
  not not_3 (not_3_out, Ctrl);
  and and_6 (and_6_out, not_3_out, SsC1);
  and and_7 (and_7_out, AsD1, Ctrl);
  not not_4 (not_4_out, Ctrl);
  and and_8 (and_8_out, not_4_out, SsD1);
  or or_1 (sA1, and_1_out, and_2_out);
  or or_2 (sB1, and_3_out, and_4_out);
  or or_3 (sC1, and_5_out, and_6_out);
  or or_4 (sD1, and_7_out, and_8_out);
  not not_5 (not_5_out, Ctrl);
  not not_6 (not_6_out, Ctrl);
  not not_7 (not_7_out, Ctrl);
  not not_8 (not_8_out, Ctrl);
  and and_9 (and_9_out, AsA2, Ctrl);
  and and_10 (and_10_out, not_5_out, SsA2);
  and and_11 (and_11_out, AsB2, Ctrl);
  and and_12 (and_12_out, not_6_out, SsB2);
  and and_13 (and_13_out, AsC2, Ctrl);
  and and_14 (and_14_out, not_7_out, SsC2);
  and and_15 (and_15_out, AsD2, Ctrl);
  and and_16 (and_16_out, not_8_out, SsD2);
  or or_5 (sA2, and_9_out, and_10_out);
  or or_6 (sB2, and_11_out, and_12_out);
  or or_7 (sC2, and_13_out, and_14_out);
  or or_8 (sD2, and_15_out, and_16_out);

  // Other names for the same wires on the sheet: iiin = Ctrl
endmodule

module AlarmM (
  input  Ctrl,
  input  AmA1,
  input  AmA2,
  input  SmA1,
  input  SmA2,
  input  AmB1,
  input  AmB2,
  input  SmB1,
  input  SmB2,
  input  AmC1,
  input  AmC2,
  input  SmC1,
  input  SmC2,
  input  AmD1,
  input  AmD2,
  input  SmD1,
  input  SmD2,
  output mA1,
  output mA2,
  output mB1,
  output mB2,
  output mC1,
  output mC2,
  output mD1,
  output mD2
);

  wire and_1_out, and_2_out, and_3_out, and_4_out, and_5_out, and_6_out, and_7_out, and_8_out, and_9_out,
       and_10_out, and_11_out, and_12_out, and_13_out, and_14_out, and_15_out, and_16_out, not_1_out,
       not_2_out, not_3_out, not_4_out, not_5_out, not_6_out, not_7_out, not_8_out;

  not not_1 (not_1_out, Ctrl);
  not not_2 (not_2_out, Ctrl);
  not not_3 (not_3_out, Ctrl);
  not not_4 (not_4_out, Ctrl);
  and and_1 (and_1_out, AmA1, Ctrl);
  and and_2 (and_2_out, not_1_out, SmA1);
  and and_3 (and_3_out, AmB1, Ctrl);
  and and_4 (and_4_out, not_2_out, SmB1);
  and and_5 (and_5_out, AmC1, Ctrl);
  and and_6 (and_6_out, not_3_out, SmC1);
  and and_7 (and_7_out, AmD1, Ctrl);
  and and_8 (and_8_out, not_4_out, SmD1);
  or or_1 (mA1, and_1_out, and_2_out);
  or or_2 (mB1, and_3_out, and_4_out);
  or or_3 (mC1, and_5_out, and_6_out);
  or or_4 (mD1, and_7_out, and_8_out);
  and and_9 (and_9_out, AmA2, Ctrl);
  not not_5 (not_5_out, Ctrl);
  and and_10 (and_10_out, not_5_out, SmA2);
  and and_11 (and_11_out, AmB2, Ctrl);
  not not_6 (not_6_out, Ctrl);
  and and_12 (and_12_out, not_6_out, SmB2);
  and and_13 (and_13_out, AmC2, Ctrl);
  not not_7 (not_7_out, Ctrl);
  and and_14 (and_14_out, not_7_out, SmC2);
  and and_15 (and_15_out, AmD2, Ctrl);
  not not_8 (not_8_out, Ctrl);
  and and_16 (and_16_out, not_8_out, SmD2);
  or or_5 (mA2, and_9_out, and_10_out);
  or or_6 (mB2, and_11_out, and_12_out);
  or or_7 (mC2, and_13_out, and_14_out);
  or or_8 (mD2, and_15_out, and_16_out);

  // Other names for the same wires on the sheet: iiin = Ctrl
endmodule

module AlarmH (
  input  Ctrl,
  input  AhA1,
  input  AhA2,
  input  ShA1,
  input  ShA2,
  input  AhB1,
  input  AhB2,
  input  ShB1,
  input  ShB2,
  input  AhC1,
  input  AhC2,
  input  ShC1,
  input  ShC2,
  input  AhD1,
  input  AhD2,
  input  ShD1,
  input  ShD2,
  output hA1,
  output hA2,
  output hB1,
  output hB2,
  output hC1,
  output hC2,
  output hD1,
  output hD2
);

  wire and_1_out, and_2_out, and_3_out, and_4_out, and_5_out, and_6_out, and_7_out, and_8_out, and_9_out,
       and_10_out, and_11_out, and_12_out, and_13_out, and_14_out, and_15_out, and_16_out, not_1_out,
       not_2_out, not_3_out, not_4_out, not_5_out, not_6_out, not_7_out, not_8_out;

  and and_1 (and_1_out, AhA1, Ctrl);
  not not_1 (not_1_out, Ctrl);
  and and_2 (and_2_out, not_1_out, ShA1);
  and and_3 (and_3_out, AhB1, Ctrl);
  not not_2 (not_2_out, Ctrl);
  and and_4 (and_4_out, not_2_out, ShB1);
  and and_5 (and_5_out, AhC1, Ctrl);
  not not_3 (not_3_out, Ctrl);
  and and_6 (and_6_out, not_3_out, ShC1);
  and and_7 (and_7_out, AhD1, Ctrl);
  not not_4 (not_4_out, Ctrl);
  and and_8 (and_8_out, not_4_out, ShD1);
  or or_1 (hA1, and_1_out, and_2_out);
  or or_2 (hB1, and_3_out, and_4_out);
  or or_3 (hC1, and_5_out, and_6_out);
  or or_4 (hD1, and_7_out, and_8_out);
  not not_5 (not_5_out, Ctrl);
  not not_6 (not_6_out, Ctrl);
  not not_7 (not_7_out, Ctrl);
  not not_8 (not_8_out, Ctrl);
  and and_9 (and_9_out, AhA2, Ctrl);
  and and_10 (and_10_out, not_5_out, ShA2);
  and and_11 (and_11_out, AhB2, Ctrl);
  and and_12 (and_12_out, not_6_out, ShB2);
  and and_13 (and_13_out, AhC2, Ctrl);
  and and_14 (and_14_out, not_7_out, ShC2);
  and and_15 (and_15_out, AhD2, Ctrl);
  and and_16 (and_16_out, not_8_out, ShD2);
  or or_5 (hA2, and_9_out, and_10_out);
  or or_6 (hB2, and_11_out, and_12_out);
  or or_7 (hC2, and_13_out, and_14_out);
  or or_8 (hD2, and_15_out, and_16_out);

  // Other names for the same wires on the sheet: iiin = Ctrl
endmodule

module Alarm1 (
  input  SA1,
  input  AA1,
  input  SB1,
  input  AB1,
  input  SC1,
  input  AC1,
  input  SD1,
  input  AP,
  input  AD1,
  input  SA2,
  input  AA2,
  input  SB2,
  input  AB2,
  input  SC2,
  input  AC2,
  input  SD2,
  input  AD2,
  output TRUE
);

  wire A, AA, and_1_out, and_2_out, B, BB, C, CC, D, DD;

  xnor xnor_1 (A, SA1, AA1);
  xnor xnor_2 (B, SB1, AB1);
  xnor xnor_3 (C, SC1, AC1);
  xnor xnor_4 (D, SD1, AD1);
  xnor xnor_5 (AA, SA2, AA2);
  xnor xnor_6 (BB, SB2, AB2);
  xnor xnor_7 (CC, SC2, AC2);
  xnor xnor_8 (DD, SD2, AD2);
  and and_1 (and_1_out, A, AA, B, BB);
  and and_2 (and_2_out, C, CC, D, DD);
  and and_3 (TRUE, and_1_out, AP, and_2_out);
endmodule

module AlarmTrue (
  input  True2,
  input  True3,
  input  True4,
  output led
);

  wire or_1_out;

  or or_1 (or_1_out, True3, True4);
  and and_1 (led, True2, or_1_out);
endmodule

module ShowAMorPM (
  input  AM1,
  input  only12,
  input  PM1,
  input  Switch,
  input  Alarm,
  output AM,
  output PM
);

  wire not_1_out, not_2_out;

  and and_1 (AM, AM1, Switch, only12, not_1_out);
  not not_1 (not_1_out, Alarm);
  and and_2 (PM, PM1, Switch, only12, not_2_out);
  not not_2 (not_2_out, Alarm);
endmodule

module j12new (
  input  in1,
  input  Reset,
  input  Switch,
  output A1,
  output B1,
  output C1,
  output D1,
  output A2,
  output B2,
  output C2,
  output D2,
  output AM,
  output PM
);

  wire add, and_2_out, and_3_out, and_4_out, Delete1, Delete2, not_1_out, not_2_out, or_1_out, or_4_out,
       set12;

  J_K_Flip_Flop #(.trigger("falling")) j_k_ff_1 (
    .J(1'b1), .K(1'b1), .clk(in1), .Q(A1), .reset(Delete1));  // open: Qn, preset
  and and_1 (add, B1, D1);
  and and_2 (and_2_out, B1, D1);
  and and_3 (and_3_out, B1, A1, A2);
  J_K_Flip_Flop #(.trigger("falling")) j_k_ff_2 (
    .J(1'b1), .K(1'b1), .clk(A1), .Q(B1), .preset(set12), .reset(or_1_out));  // open: Qn
  or or_1 (or_1_out, Delete1, Delete2);
  or or_2 (Delete1, Reset, and_2_out);
  J_K_Flip_Flop #(.trigger("falling")) j_k_ff_3 (
    .J(1'b1), .K(1'b1), .clk(B1), .Q(C1), .reset(or_4_out));  // open: Qn, preset
  or or_3 (Delete2, Reset, and_3_out);
  J_K_Flip_Flop #(.trigger("falling")) j_k_ff_4 (
    .J(1'b1), .K(1'b1), .clk(C1), .Q(D1), .reset(Delete1));  // open: Qn, preset
  or or_4 (or_4_out, Delete1, Delete2);
  D_Flip_Flop d_ff_1 (.D(1'b1), .clk(Switch), .Q(set12), .reset(set12));  // open: Qn, preset
  J_K_Flip_Flop j_k_ff_5 (.J(1'b1), .K(1'b1), .clk(add), .Q(A2), .preset(set12), .reset(Delete2));  // open: Qn
  not not_1 (not_1_out, A2);
  not not_2 (not_2_out, not_1_out);
  J_K_Flip_Flop #(.trigger("falling")) j_k_ff_6 (.J(1'b1), .K(1'b1), .Q(B2));  // open: clk, Qn, preset, reset
  J_K_Flip_Flop #(.trigger("falling")) j_k_ff_7 (.J(1'b1), .K(1'b1), .clk(B2), .Q(C2));  // open: Qn, preset, reset
  and and_4 (and_4_out, B1, not_2_out);
  J_K_Flip_Flop #(.trigger("falling")) j_k_ff_8 (.J(1'b1), .K(1'b1), .clk(C2), .Q(D2));  // open: Qn, preset, reset
  J_K_Flip_Flop j_k_ff_9 (.J(1'b1), .K(1'b1), .clk(and_4_out), .Q(AM), .Qn(PM));  // open: preset, reset

  // Other names for the same wires on the sheet: add1 = B1; add2 = D1; add3 = A1; add4 = A2; Reset001 = Reset
endmodule
